// Logisim project SimpleCPU.circ as structural Verilog: 11 circuits, main circuit main
module main (
);

  wire controlunit_1_ip_we, controlunit_1_ram_we, controlunit_1_reg_we, flow_1_flow_ip_we, not_1_out,
       programClock_out, ResetCounter, ResetRegisters;
  wire [3:0] controlunit_1_index, controlunit_1_out_val, controlunit_1_out_val_2, flow_1_outval,
       instructioncounter_1_count, registersv2_1_areg, registersv2_1_areg_2;
  wire [7:0] alu_1_outval, controlunit_1_a_out, controlunit_1_a_reg, controlunit_1_b_out,
       controlunit_1_b_reg, controlunit_1_c_out, controlunit_1_c_reg, logic_1_outval, memory_1_outval,
       ram_1_dout, registersv2_1_breg, registersv2_1_creg;
  wire [31:0] rom_1_data;

  Clock programClock (.out(programClock_out));
  not not_1 (not_1_out, programClock_out);
  Button button_1 (.out(ResetCounter));
  RAM ram_1 (
    .addr(controlunit_1_a_reg), .we(controlunit_1_ram_we), .oe(1'b1), .clk(not_1_out),
    .din({controlunit_1_out_val_2, controlunit_1_out_val}), .dout(ram_1_dout));
  Button button_2 (.out(ResetRegisters));
  ROM #(.addrWidth(4), .dataWidth(32)) rom_1 (.addr(instructioncounter_1_count), .data(rom_1_data));
  InstructionCounter instructioncounter_1 (
    .value(controlunit_1_out_val), .set(controlunit_1_ip_we), .clock(programClock_out), .reset(ResetCounter),
    .count(instructioncounter_1_count));
  ControlUnit controlunit_1 (
    .OpCode(rom_1_data[31:24]), .A_in(rom_1_data[23:16]), .B_in(rom_1_data[15:8]), .C_in(rom_1_data[7:0]),
    .ALU_val(alu_1_outval), .LOGIC_val(logic_1_outval), .FLOW_val(flow_1_outval),
    .MEMORY_val(memory_1_outval), .RAM_in(ram_1_dout),
    .A_reg_val({registersv2_1_areg_2, registersv2_1_areg}), .B_reg_val(registersv2_1_breg),
    .C_reg_val(registersv2_1_creg), .FLOW_IP_WE(flow_1_flow_ip_we), .index(controlunit_1_index),
    .A_out(controlunit_1_a_out), .B_out(controlunit_1_b_out), .C_out(controlunit_1_c_out),
    .A_reg(controlunit_1_a_reg), .B_reg(controlunit_1_b_reg), .C_reg(controlunit_1_c_reg),
    .Out_val({controlunit_1_out_val_2, controlunit_1_out_val}), .Reg_WE(controlunit_1_reg_we),
    .IP_WE(controlunit_1_ip_we), .RAM_WE(controlunit_1_ram_we));
  registersv2 registersv2_1 (
    .Aaddr(controlunit_1_a_reg), .Baddr(controlunit_1_b_reg), .Caddr(controlunit_1_c_reg),
    .Value({controlunit_1_out_val_2, controlunit_1_out_val}), .WE(controlunit_1_reg_we), .clock(not_1_out),
    .reset(ResetRegisters), .Areg({registersv2_1_areg_2, registersv2_1_areg}), .Breg(registersv2_1_breg),
    .Creg(registersv2_1_creg));
  Hex_Digit_Display hex_digit_display_1 (.value(registersv2_1_areg_2));  // open: dp
  Hex_Digit_Display hex_digit_display_2 (.value(registersv2_1_areg));  // open: dp
  ALU alu_1 (
    .index(controlunit_1_index), .A_in(controlunit_1_a_out), .B_in(controlunit_1_b_out),
    .C_in(controlunit_1_c_out), .outVal(alu_1_outval));
  LOGIC logic_1 (
    .index(controlunit_1_index), .A_in(controlunit_1_a_out), .B_in(controlunit_1_b_out),
    .C_in(controlunit_1_c_out), .outVal(logic_1_outval));
  FLOW flow_1 (
    .index(controlunit_1_index), .A_in(controlunit_1_a_out), .B_in(controlunit_1_b_out),
    .C_in(controlunit_1_c_out), .outVal(flow_1_outval), .FLOW_IP_WE(flow_1_flow_ip_we));
  MEMORY memory_1 (
    .index(controlunit_1_index), .A_in(controlunit_1_a_out), .B_in(controlunit_1_b_out),
    .C_in(controlunit_1_c_out), .outVal(memory_1_outval));

  // Notes on the sheet:
  //   starts high
  //   contents of rom_1 (hex, n*v repeats v):
  //   4000fe00
endmodule

module fulladder (
  input  a,
  input  b,
  input  carryin,
  output carryout,
  output sum
);

  wire n7408_1_pin3, n7408_1_pin4, n7408_1_pin6;

  _7408 #(.ShowInternalStructure("true")) u_7408_1 (
    .pin1(a), .pin2(b), .pin3(n7408_1_pin3), .pin4(n7408_1_pin4), .pin5(carryin), .pin6(n7408_1_pin6));  // open: pin13, pin12, pin11, pin10, pin9, pin8
  _7486 #(.ShowInternalStructure("true")) u_7486_1 (
    .pin13(b), .pin12(a), .pin11(n7408_1_pin4), .pin10(n7408_1_pin4), .pin9(carryin), .pin8(sum));  // open: pin1, pin2, pin3, pin4, pin5, pin6
  _7432 #(.ShowInternalStructure("true")) u_7432_1 (
    .pin1(n7408_1_pin6), .pin2(n7408_1_pin3), .pin3(carryout));  // open: pin4, pin5, pin6, pin13, pin12, pin11, pin10, pin9, pin8
endmodule

module ALU (
  input  [3:0] index,
  input  [7:0] A_in,
  input  [7:0] B_in,
  input  [7:0] C_in,
  output [7:0] outVal
);

  wire [0:0] undriven;
  wire [7:0] adder_1_out, comparator_1_eq, comparator_1_gt, comparator_1_lt, divider_1_out, multiplier_1_out,
       subtractor_1_out;
  wire [7:7] undriven_2;

  Adder adder_1 (.a(B_in), .b(C_in), .out(adder_1_out));  // open: cin, cout
  Subtractor subtractor_1 (.a(B_in), .b(C_in), .out(subtractor_1_out));  // open: bin, bout
  Multiplier multiplier_1 (.a(B_in), .b(C_in), .out(multiplier_1_out));  // open: cin, cout
  Divider divider_1 (.a(B_in), .b(C_in), .out(divider_1_out));  // open: upper, rem
  Comparator comparator_1 (
    .a(B_in), .b(C_in), .gt(comparator_1_gt[0]), .eq(comparator_1_eq[0]), .lt(comparator_1_lt[0]));
  Multiplexer #(.select(4), .width(8)) multiplexer_1 (
    .in0(adder_1_out), .in1(subtractor_1_out), .in2(multiplier_1_out), .in3(divider_1_out),
    .in4({B_in[6:0], undriven[0]}), .in5({undriven_2[7], B_in[7:1]}), .in6(comparator_1_gt),
    .in7(comparator_1_eq), .in8(comparator_1_lt), .out(outVal), .sel(index));  // open: in9, in10, in11, in12, in13, in14, in15
endmodule

module InstructionCounter (
  input  [3:0] value,
  input  set,
  input  clock,
  input  reset,
  output [3:0] count
);

  wire and_1_out, and_2_out, and_3_out, and_4_out, and_5_out, and_6_out, and_7_out, and_8_out, j_k_ff_1_qn,
       not_1_out, not_2_out, not_3_out, not_4_out, or_1_out, or_2_out, or_3_out, or_4_out, t_ff_1_qn,
       t_ff_2_qn, t_ff_3_qn, undriven;

  not not_1 (not_1_out, value[1]);
  not not_2 (not_2_out, value[2]);
  not not_3 (not_3_out, value[3]);
  not not_4 (not_4_out, value[0]);
  T_Flip_Flop t_ff_1 (.T(1'b1), .clk(clock), .Q(count[0]), .Qn(t_ff_1_qn), .reset(or_1_out), .preset(and_2_out));
  and and_1 (and_1_out, set, not_4_out);
  or or_1 (or_1_out, and_1_out, reset);
  J_K_Flip_Flop j_k_ff_1 (.J(1'b1), .K(1'b1), .clk(undriven), .Qn(j_k_ff_1_qn));  // open: Q, preset, reset
  and and_2 (and_2_out, value[0], set);
  T_Flip_Flop t_ff_2 (.T(1'b1), .clk(t_ff_1_qn), .Q(count[1]), .Qn(t_ff_2_qn), .reset(or_2_out), .preset(and_4_out));
  or or_2 (or_2_out, and_3_out, reset);
  and and_3 (and_3_out, set, not_1_out);
  and and_4 (and_4_out, value[1], set);
  T_Flip_Flop t_ff_3 (.T(1'b1), .clk(t_ff_2_qn), .Q(count[2]), .Qn(t_ff_3_qn), .reset(or_3_out), .preset(and_6_out));
  or or_3 (or_3_out, and_5_out, reset);
  and and_5 (and_5_out, set, not_2_out);
  J_K_Flip_Flop j_k_ff_2 (.J(1'b1), .K(1'b1), .clk(j_k_ff_1_qn));  // open: Q, Qn, preset, reset
  and and_6 (and_6_out, value[2], set);
  T_Flip_Flop t_ff_4 (.T(1'b1), .clk(t_ff_3_qn), .Q(count[3]), .reset(or_4_out), .preset(and_8_out));  // open: Qn
  or or_4 (or_4_out, and_7_out, reset);
  and and_7 (and_7_out, set, not_3_out);
  and and_8 (and_8_out, value[3], set);
endmodule

module registers (
  input  [1:0] A,
  input  [1:0] B,
  input  [7:0] WriteAVal,
  input  [7:0] WriteBVal,
  input  clock,
  input  WEa,
  input  WEb,
  output [7:0] Aout,
  output [7:0] Bout
);

  wire demultiplexer_1_out0, demultiplexer_1_out1, demultiplexer_1_out2, demultiplexer_1_out3,
       demultiplexer_2_out0, demultiplexer_2_out1, demultiplexer_2_out2, demultiplexer_2_out3, or_1_out,
       or_2_out, or_3_out, or_4_out;
  wire [7:0] demultiplexer_3_out0, demultiplexer_3_out1, demultiplexer_3_out2, demultiplexer_3_out3,
       demultiplexer_4_out0, demultiplexer_4_out1, demultiplexer_4_out2, demultiplexer_4_out3, or_5_out,
       or_6_out, or_7_out, or_8_out, register_1_q, register_2_q, register_3_q, register_4_q;

  Demultiplexer #(.select(2)) demultiplexer_1 (
    .out0(demultiplexer_1_out0), .out1(demultiplexer_1_out1), .out2(demultiplexer_1_out2),
    .out3(demultiplexer_1_out3), .in(WEb), .sel(B));
  Demultiplexer #(.select(2)) demultiplexer_2 (
    .out0(demultiplexer_2_out0), .out1(demultiplexer_2_out1), .out2(demultiplexer_2_out2),
    .out3(demultiplexer_2_out3), .in(WEa), .sel(A));
  Demultiplexer #(.select(2), .width(8)) demultiplexer_3 (
    .out0(demultiplexer_3_out0), .out1(demultiplexer_3_out1), .out2(demultiplexer_3_out2),
    .out3(demultiplexer_3_out3), .in(WriteAVal), .sel(A));
  Demultiplexer #(.select(2), .width(8)) demultiplexer_4 (
    .out0(demultiplexer_4_out0), .out1(demultiplexer_4_out1), .out2(demultiplexer_4_out2),
    .out3(demultiplexer_4_out3), .in(WriteBVal), .sel(B));
  or or_1 (or_1_out, demultiplexer_1_out0, demultiplexer_2_out0);
  or or_2 (or_2_out, demultiplexer_1_out1, demultiplexer_2_out1);
  or or_3 (or_3_out, demultiplexer_1_out2, demultiplexer_2_out2);
  or or_4 (or_4_out, demultiplexer_1_out3, demultiplexer_2_out3);
  assign or_5_out = demultiplexer_3_out0 | demultiplexer_4_out0;  // OR_Gate or_5, 8 bits wide
  assign or_6_out = demultiplexer_3_out2 | demultiplexer_4_out2;  // OR_Gate or_6, 8 bits wide
  assign or_7_out = demultiplexer_3_out3 | demultiplexer_4_out3;  // OR_Gate or_7, 8 bits wide
  Register register_1 (.D(or_5_out), .en(or_1_out), .clk(clock), .Q(register_1_q));  // open: clr
  assign or_8_out = demultiplexer_3_out1 | demultiplexer_4_out1;  // OR_Gate or_8, 8 bits wide
  Register register_2 (.D(or_8_out), .en(or_2_out), .clk(clock), .Q(register_2_q));  // open: clr
  Register register_3 (.D(or_6_out), .en(or_3_out), .clk(clock), .Q(register_3_q));  // open: clr
  Register register_4 (.D(or_7_out), .en(or_4_out), .clk(clock), .Q(register_4_q));  // open: clr
  Multiplexer #(.select(2), .width(8)) multiplexer_1 (
    .in0(register_1_q), .in1(register_2_q), .in2(register_3_q), .in3(register_4_q), .out(Aout), .sel(A));
  Multiplexer #(.select(2), .width(8)) multiplexer_2 (
    .in0(register_1_q), .in1(register_2_q), .in2(register_3_q), .in3(register_4_q), .out(Bout), .sel(B));
endmodule

module registersv2 (
  input  [7:0] Aaddr,
  input  [7:0] Baddr,
  input  [7:0] Caddr,
  input  [7:0] Value,
  input  WE,
  input  clock,
  input  reset,
  output [7:0] Areg,
  output [7:0] Breg,
  output [7:0] Creg
);

  wire demultiplexer_1_out0, demultiplexer_1_out1, demultiplexer_1_out2, demultiplexer_1_out3,
       demultiplexer_1_out4, demultiplexer_1_out5, demultiplexer_1_out6, demultiplexer_1_out7;
  wire [7:0] register_1_q, register_2_q, register_3_q, register_4_q, register_5_q, register_6_q,
       register_7_q, register_8_q, register_9_q;

  Demultiplexer #(.select(4)) demultiplexer_1 (
    .out0(demultiplexer_1_out0), .out1(demultiplexer_1_out1), .out2(demultiplexer_1_out2),
    .out3(demultiplexer_1_out3), .out4(demultiplexer_1_out4), .out5(demultiplexer_1_out5),
    .out6(demultiplexer_1_out6), .out7(demultiplexer_1_out7), .in(WE), .sel(Aaddr[3:0]));  // open: out8, out9, out10, out11, out12, out13, out14, out15
  Register register_1 (.D(Value), .en(demultiplexer_1_out0), .clk(clock), .Q(register_1_q), .clr(reset));
  Register register_2 (.D(Value), .en(demultiplexer_1_out1), .clk(clock), .Q(register_2_q), .clr(reset));
  Register register_3 (.D(Value), .en(demultiplexer_1_out2), .clk(clock), .Q(register_3_q), .clr(reset));
  Register register_4 (.D(Value), .en(demultiplexer_1_out3), .clk(clock), .Q(register_4_q), .clr(reset));
  Register register_5 (.D(Value), .en(demultiplexer_1_out4), .clk(clock), .Q(register_5_q), .clr(reset));
  Register register_6 (.D(Value), .en(demultiplexer_1_out5), .clk(clock), .Q(register_6_q), .clr(reset));
  Register register_7 (.D(Value), .en(demultiplexer_1_out6), .clk(clock), .Q(register_7_q), .clr(reset));
  Register register_8 (.D(Value), .en(demultiplexer_1_out7), .clk(clock), .Q(register_8_q), .clr(reset));
  Register register_9 (.D(Value), .en(demultiplexer_1_out7), .clk(clock), .Q(register_9_q), .clr(reset));
  Multiplexer #(.select(4), .width(8)) multiplexer_1 (
    .in0(register_1_q), .in1(register_2_q), .in2(register_3_q), .in3(register_4_q), .in4(register_5_q),
    .in5(register_6_q), .in6(register_7_q), .in7(register_8_q), .in8(register_9_q), .out(Areg),
    .sel(Aaddr[3:0]));  // open: in9, in10, in11, in12, in13, in14, in15
  Multiplexer #(.select(4), .width(8)) multiplexer_2 (
    .in0(register_1_q), .in1(register_2_q), .in2(register_3_q), .in3(register_4_q), .in4(register_5_q),
    .in5(register_6_q), .in6(register_7_q), .in7(register_8_q), .in8(register_9_q), .in9({8{1'b1}}),
    .in10({8{1'b1}}), .in11({8{1'b1}}), .in12({8{1'b1}}), .in13({8{1'b1}}), .in14({8{1'b1}}),
    .in15({8{1'b1}}), .out(Breg), .sel(Baddr[3:0]));
  Multiplexer #(.select(4), .width(8)) multiplexer_3 (
    .in0(register_1_q), .in1(register_2_q), .in2(register_3_q), .in3(register_4_q), .in4(register_5_q),
    .in5(register_6_q), .in6(register_7_q), .in7(register_8_q), .in8(register_9_q), .out(Creg),
    .sel(Caddr[3:0]));  // open: in9, in10, in11, in12, in13, in14, in15

  // Notes on the sheet:
  //   0x09
endmodule

module ControlUnit (
  input  [7:0] OpCode,
  input  [7:0] A_in,
  input  [7:0] B_in,
  input  [7:0] C_in,
  input  [7:0] ALU_val,
  input  [7:0] LOGIC_val,
  input  [3:0] FLOW_val,
  input  [7:0] MEMORY_val,
  input  [7:0] RAM_in,
  input  [7:0] A_reg_val,
  input  [7:0] B_reg_val,
  input  [7:0] C_reg_val,
  input  FLOW_IP_WE,
  output [3:0] index,
  output [7:0] A_out,
  output [7:0] B_out,
  output [7:0] C_out,
  output [7:0] A_reg,
  output [7:0] B_reg,
  output [7:0] C_reg,
  output [7:0] Out_val,
  output Reg_WE,
  output IP_WE,
  output RAM_WE
);

  wire multiplexer_4_out, multiplexer_11_out;
  wire [7:0] multiplexer_1_out, multiplexer_2_out, multiplexer_3_out, multiplexer_5_out;

  Multiplexer #(.select(3), .width(8)) multiplexer_1 (
    .in0(A_in), .in1(A_in), .out(multiplexer_1_out), .sel(OpCode[2:0]));  // open: in2, in3, in4, in5, in6, in7
  Multiplexer #(.select(3), .width(8)) multiplexer_2 (
    .in0(B_in), .in1(B_reg_val), .out(multiplexer_2_out), .sel(OpCode[2:0]));  // open: in2, in3, in4, in5, in6, in7
  Multiplexer #(.select(3), .width(8)) multiplexer_3 (
    .out(multiplexer_3_out), .sel(OpCode[2:0]));  // open: in0, in1, in2, in3, in4, in5, in6, in7
  Multiplexer #(.select(3)) multiplexer_4 (
    .in0(1'b1), .in1(1'b1), .out(multiplexer_4_out), .sel(OpCode[2:0]));  // open: in2, in3, in4, in5, in6, in7
  Multiplexer #(.select(2), .width(8)) multiplexer_5 (
    .in0(A_in), .in1(A_in), .in2(A_in), .in3(A_reg_val), .out(multiplexer_5_out));  // open: sel
  Multiplexer #(.select(3), .width(8)) multiplexer_6 (
    .in0({8{1'b0}}), .in1(A_reg_val), .in2(A_reg_val), .in3(multiplexer_5_out), .in4(multiplexer_1_out),
    .out(A_out), .sel(OpCode[6:4]));  // open: in5, in6, in7
  Multiplexer #(.select(3), .width(8)) multiplexer_7 (
    .in0({8{1'b0}}), .in1(B_reg_val), .in2(B_reg_val), .in3(B_reg_val), .in4(multiplexer_2_out), .out(B_out),
    .sel(OpCode[6:4]));  // open: in5, in6, in7
  Multiplexer #(.select(3), .width(8)) multiplexer_8 (
    .in0({8{1'b0}}), .in1(C_reg_val), .in2(C_reg_val), .in3(C_reg_val), .in4(multiplexer_3_out), .out(C_out),
    .sel(OpCode[6:4]));  // open: in5, in6, in7
  Multiplexer #(.select(3), .width(8)) multiplexer_9 (
    .in0({8{1'b0}}), .in1(ALU_val), .in2(LOGIC_val), .in3({4'b0000, FLOW_val}), .in4(MEMORY_val),
    .out(Out_val), .sel(OpCode[6:4]));  // open: in5, in6, in7
  Multiplexer #(.select(3)) multiplexer_10 (
    .in0(1'b0), .in1(1'b1), .in2(1'b0), .in3(multiplexer_4_out), .out(Reg_WE), .sel(OpCode[6:4]));  // open: in4, in5, in6, in7
  Multiplexer #(.select(3)) multiplexer_11 (
    .in0(1'b0), .in1(1'b0), .in2(1'b0), .in3(1'b1), .out(multiplexer_11_out), .sel(OpCode[6:4]));  // open: in4, in5, in6, in7
  Multiplexer #(.select(3)) multiplexer_12 (
    .in0(1'b0), .in1(1'b0), .in2(1'b0), .out(RAM_WE), .sel(OpCode[6:4]));  // open: in3, in4, in5, in6, in7
  and and_1 (IP_WE, multiplexer_11_out, FLOW_IP_WE);

  assign A_reg = A_in;
  assign B_reg = B_in;
  assign C_reg = C_in;
  assign index = OpCode[3:0];
endmodule

module OneHotState (
  input  clock,
  output Fetch,
  output Decode,
  output Execute,
  output Advance
);

  wire t_ff_1_qn;
  wire [1:0] t_ff_1_q;

  T_Flip_Flop t_ff_1 (.T(1'b1), .clk(clock), .Q(t_ff_1_q[0]), .Qn(t_ff_1_qn));  // open: reset, preset
  T_Flip_Flop t_ff_2 (.T(1'b1), .clk(t_ff_1_qn), .Q(t_ff_1_q[1]));  // open: Qn, reset, preset
  Demultiplexer #(.select(2)) demultiplexer_1 (
    .out0(Fetch), .out1(Decode), .out2(Execute), .out3(Advance), .in(1'b1), .sel(t_ff_1_q));
endmodule

module FLOW (
  input  [3:0] index,
  input  [7:0] A_in,
  input  [7:0] B_in,
  input  [7:0] C_in,
  output [3:0] outVal,
  output FLOW_IP_WE
);

  wire comparator_1_eq;

  Comparator comparator_1 (.a(B_in), .b({8{1'b0}}), .eq(comparator_1_eq));  // open: gt, lt
  Multiplexer #(.select(2)) multiplexer_1 (
    .in0(1'b1), .in1(comparator_1_eq), .in2(1'b1), .out(FLOW_IP_WE));  // open: in3, sel

  assign outVal = A_in[3:0];

  // Notes on the sheet:
  //   label address
endmodule

module MEMORY (
  input  [3:0] index,
  input  [7:0] A_in,
  input  [7:0] B_in,
  input  [7:0] C_in,
  output [7:0] outVal
);

  Multiplexer #(.select(4), .width(8)) multiplexer_1 (
    .in0(B_in), .in2(B_in), .in3(B_in), .out(outVal), .sel(index));  // open: in1, in4, in5, in6, in7, in8, in9, in10, in11, in12, in13, in14, in15

  // Notes on the sheet:
  //   r1
  //   r2
  //   set
  //   addr
  //   val
endmodule

module LOGIC (
  input  [3:0] index,
  input  [7:0] A_in,
  input  [7:0] B_in,
  input  [7:0] C_in,
  output [7:0] outVal
);

  wire [7:0] and_1_out, nand_1_out, nor_1_out, not_1_out, or_1_out, shifter_1_out, xor_1_out;

  assign not_1_out = ~B_in;  // NOT_Gate not_1, 8 bits wide
  assign and_1_out = B_in & C_in;  // AND_Gate and_1, 8 bits wide
  assign or_1_out = B_in | C_in;  // OR_Gate or_1, 8 bits wide
  assign nor_1_out = ~(B_in | C_in);  // NOR_Gate nor_1, 8 bits wide
  assign nand_1_out = ~(B_in & C_in);  // NAND_Gate nand_1, 8 bits wide
  assign xor_1_out = B_in ^ C_in;  // XOR_Gate xor_1, 8 bits wide
  Shifter shifter_1 (.in(B_in), .\dist (C_in[2:0]), .out(shifter_1_out));
  Multiplexer #(.select(4), .width(8)) multiplexer_1 (
    .in0(not_1_out), .in1(and_1_out), .in2(or_1_out), .in3(nor_1_out), .in4(nand_1_out), .in5(xor_1_out),
    .in6(shifter_1_out), .out(outVal), .sel(index));  // open: in7, in8, in9, in10, in11, in12, in13, in14, in15
endmodule
